// Logisim project 150117057_150117034_150116010_PS3.circ as structural Verilog: 15 circuits, main circuit main
// readRegisterData1
module main (
  input  in_1,
  input  in_2,
  input  Reset,
  input  in_4,
  input  in_5,
  input  in_6,
  input  in_7,
  input  Branch,
  input  Clear,
  input  Clear_2,
  output [2:0] out_11,
  output [2:0] out_12,
  output [15:0] RegisterData1,
  output [15:0] Instruction,
  output [2:0] out_15,
  output [15:0] ReadRegisterData2,
  output [15:0] out_17,
  output [9:0] Adress,
  output [15:0] out_19,
  output [15:0] Instruction_2,
  output [9:0] out_21,
  output [15:0] out_22,
  output [15:0] Instruction_3
);

  wire ALUControl, ALUEnable, CMPsig, DataMemRead, DataMemWrite, IMM6SIGNAL, \İnstRead , JA, JAE, JB, JBE,
       JE, JumpSignal, LDsignal, PCREAD, Regread, RegWrite, STsignal, undriven, undriven_2;
  wire [2:0] multiplexer_1_out;
  wire [5:0] IMM6;
  wire [15:0] alu_1_result, multiplexer_2_out, multiplexer_3_out, register_file_1_register1data,
       register_file_1_register2data;

  Control_Unit control_unit_1 (
    .clock(in_1), .dataMemWrite(DataMemWrite), .\İnstRead (\İnstRead ), .PCRead(PCREAD), .RegRead(Regread),
    .ALUEnable(ALUEnable), .RegWrite(RegWrite), .Instruction(Instruction), .DR(out_11), .SR1(out_12),
    .SR2(out_15), .IMM6(IMM6), ._10_BIT_ADDRESS(Adress), .ALUcontrol(ALUControl), .DataMemRead(DataMemRead),
    .STSignal(STsignal), .LDsignal(LDsignal), .CMPsig(CMPsig), .JumpSignal(JumpSignal),
    .IMM6SIGNAL(IMM6SIGNAL), .JAIN(JA), .JEIN(JE), .JBIN(JB), .JAEIN(JAE), .JBEIN(JBE));
  jmp jmp_1 (
    .JUMP_ADDRESS(Adress), .ADDRSelect(JumpSignal), .Enable(PCREAD), .Clock(in_1), .Clear(Clear),
    .BranchSignal(Branch), .out_7(out_21));
  ROM #(.addrWidth(10), .dataWidth(16)) rom_1 (.addr(out_21), .data(Instruction_2), .sel(undriven));
  Register #(.width(16), .trigger("high")) register_1 (
    .D(Instruction_2), .en(\İnstRead ), .Q(Instruction), .clk(in_1), .clr(Clear_2));
  Multiplexer #(.width(3), .enable("false")) multiplexer_1 (
    .in0(out_12), .in1(out_11), .out(multiplexer_1_out), .sel(STsignal));
  Multiplexer #(.width(16), .enable("false")) multiplexer_2 (
    .in0(out_19), .in1(out_17), .out(multiplexer_2_out), .sel(LDsignal));
  assign out_22 = {{10{IMM6[5]}}, IMM6};  // Bit_Extender bit_extender_1
  Multiplexer #(.width(16), .enable("false")) multiplexer_3 (
    .in0(ReadRegisterData2), .in1(out_22), .out(multiplexer_3_out), .sel(IMM6SIGNAL));
  Register_File register_file_1 (
    .write(out_11), .read_register_1(multiplexer_1_out), .read_register_2(out_15),
    .register1data(register_file_1_register1data), .register2data(register_file_1_register2data),
    .input_data(multiplexer_2_out), .Register_Write(RegWrite), .clock(in_1), .Reset(Reset));
  Register #(.width(16), .trigger("high")) register_2 (
    .D(register_file_1_register1data), .en(Regread), .Q(RegisterData1), .clk(in_1), .clr(in_2));
  Register #(.width(16), .trigger("high")) register_3 (
    .D(register_file_1_register2data), .en(Regread), .Q(ReadRegisterData2), .clk(in_1), .clr(in_5));
  ALU alu_1 (
    .a(RegisterData1), .b(multiplexer_3_out), .Result(alu_1_result), .AluControl(ALUControl), .ALUENABLE(in_1));
  Register #(.width(16), .trigger("high")) register_4 (
    .D(alu_1_result), .en(ALUEnable), .Q(out_19), .clk(in_1), .clr(in_7));
  _16_Bit_Comparator u_16_bit_comparator_1 (
    .OP1(RegisterData1), .OP2(ReadRegisterData2), .CmpEnable(CMPsig), .Clear(in_6), .Clock(in_1), .JA(JA),
    .JE(JE), .JAE(JAE), .JB(JB), .JBE(JBE));
  RAM #(.addrWidth(10), .dataWidth(16), .bus("separate")) ram_1 (
    .addr(Adress), .din(RegisterData1), .data(out_17), .str(DataMemWrite), .sel(undriven_2), .clk(in_1),
    .ld(DataMemRead), .clr(in_4));

  assign Instruction_3 = Instruction;

  // Other names for the same wires on the sheet: CLOCK = in_1; DR[2:0] = out_11; Memout[15:0] = out_17;
  //   Result[15:0] = out_19; SRC1[2:0] = out_12; SRC1data[15:0] = RegisterData1; SRC2[2:0] = out_15;
  //   SRC2DATA[15:0] = ReadRegisterData2

  // Notes on the sheet:
  //   contents of rom_1 (hex, n*v repeats v):
  //   6000 6401 6802 6c03 7004 c003 e403 c082 f404 20c5 c001 e002 2801 2d01 c084 ec02 9005 5001 c184 e801
  //   4d47 9005 a3ea
endmodule

// HA
module Half_Adder (
  input  b,
  input  a,
  output Sum,
  output COut
);

  xor xor_1 (Sum, b, a);
  and and_1 (COut, b, a);
endmodule

// FA
module Full_Adder (
  input  C_in,
  input  a,
  input  b,
  output S,
  output COut
);

  wire and_1_out, and_2_out, xor_1_out;

  xor xor_1 (xor_1_out, a, b);
  and and_1 (and_1_out, C_in, xor_1_out);
  and and_2 (and_2_out, a, b);
  xor xor_2 (S, C_in, xor_1_out);
  or or_1 (COut, and_1_out, and_2_out);
endmodule

// 16B+
module _16_Bit_Adder (
  input  [15:0] a,
  input  [15:0] b,
  output [15:0] Result,
  output COut
);

  wire Full_Adder_2_cout, Full_Adder_3_cout, Full_Adder_4_cout, Full_Adder_5_cout, Full_Adder_6_cout,
       Full_Adder_7_cout, Full_Adder_8_cout, Full_Adder_9_cout, Full_Adder_10_cout, Full_Adder_11_cout,
       Full_Adder_12_cout, Full_Adder_13_cout, Full_Adder_14_cout, Full_Adder_cout, half_adder_1_cout;

  Half_Adder half_adder_1 (.b(b[0]), .a(a[0]), .Sum(Result[0]), .COut(half_adder_1_cout));
  Full_Adder Full_Adder (.C_in(half_adder_1_cout), .a(b[1]), .b(a[1]), .S(Result[1]), .COut(Full_Adder_cout));
  Full_Adder Full_Adder_2 (.C_in(Full_Adder_cout), .a(b[2]), .b(a[2]), .S(Result[2]), .COut(Full_Adder_2_cout));
  Full_Adder Full_Adder_3 (.C_in(Full_Adder_2_cout), .a(b[3]), .b(a[3]), .S(Result[3]), .COut(Full_Adder_3_cout));
  Full_Adder Full_Adder_4 (.C_in(Full_Adder_3_cout), .a(b[4]), .b(a[4]), .S(Result[4]), .COut(Full_Adder_4_cout));
  Full_Adder Full_Adder_5 (.C_in(Full_Adder_4_cout), .a(b[5]), .b(a[5]), .S(Result[5]), .COut(Full_Adder_5_cout));
  Full_Adder Full_Adder_6 (.C_in(Full_Adder_5_cout), .a(b[6]), .b(a[6]), .S(Result[6]), .COut(Full_Adder_6_cout));
  Full_Adder Full_Adder_7 (.C_in(Full_Adder_6_cout), .a(b[7]), .b(a[7]), .S(Result[7]), .COut(Full_Adder_7_cout));
  Full_Adder Full_Adder_8 (.C_in(Full_Adder_7_cout), .a(b[8]), .b(a[8]), .S(Result[8]), .COut(Full_Adder_8_cout));
  Full_Adder Full_Adder_9 (.C_in(Full_Adder_8_cout), .a(b[9]), .b(a[9]), .S(Result[9]), .COut(Full_Adder_9_cout));
  Full_Adder Full_Adder_10 (.C_in(Full_Adder_9_cout), .a(b[10]), .b(a[10]), .S(Result[10]), .COut(Full_Adder_10_cout));
  Full_Adder Full_Adder_11 (.C_in(Full_Adder_10_cout), .a(b[11]), .b(a[11]), .S(Result[11]), .COut(Full_Adder_11_cout));
  Full_Adder Full_Adder_12 (.C_in(Full_Adder_11_cout), .a(b[12]), .b(a[12]), .S(Result[12]), .COut(Full_Adder_12_cout));
  Full_Adder Full_Adder_13 (.C_in(Full_Adder_12_cout), .a(b[13]), .b(a[13]), .S(Result[13]), .COut(Full_Adder_13_cout));
  Full_Adder Full_Adder_14 (.C_in(Full_Adder_13_cout), .a(b[14]), .b(a[14]), .S(Result[14]), .COut(Full_Adder_14_cout));
  Full_Adder Full_Adder_15 (.C_in(Full_Adder_14_cout), .a(b[15]), .b(a[15]), .S(Result[15]), .COut(COut));
endmodule

// CMP
module Comparator (
  input  a,
  input  b,
  input  EQ_IN,
  input  GT_IN,
  input  LT_IN,
  output EQ_OUT,
  output GT_OUT,
  output LT_OUT
);

  wire and_1_out, and_2_out, not_1_out, not_2_out, xnor_1_out;

  not not_1 (not_1_out, b);
  not not_2 (not_2_out, a);
  xnor xnor_1 (xnor_1_out, a, b);
  and and_1 (and_1_out, a, not_1_out, EQ_IN);
  and and_2 (and_2_out, not_2_out, b, EQ_IN);
  and and_3 (EQ_OUT, xnor_1_out, EQ_IN);
  or or_1 (GT_OUT, and_1_out, GT_IN);
  or or_2 (LT_OUT, and_2_out, LT_IN);
endmodule

// CMP
module _16_Bit_Comparator (
  input  [15:0] OP1,
  input  [15:0] OP2,
  input  CmpEnable,
  input  Clear,
  input  Clock,
  output JA,
  output JE,
  output JAE,
  output JB,
  output JBE
);

  wire and_1_out, and_2_out, and_3_out, CF, not_1_out, not_2_out, or_1_out, ZF;

  Comparator_part #(.width(16)) comparator_1 (.a(OP1), .b(OP2), .eq(ZF), .lt(CF));  // open: gt
  not not_1 (not_1_out, ZF);
  not not_2 (not_2_out, CF);
  and and_1 (and_1_out, not_1_out, not_2_out);
  and and_2 (and_2_out, ZF, not_2_out);
  and and_3 (and_3_out, CF, not_1_out);
  or or_1 (or_1_out, ZF, CF);
  Register #(.width(1), .trigger("high")) register_1 (.D(and_1_out), .en(CmpEnable), .Q(JA), .clk(Clock), .clr(Clear));
  Register #(.width(1), .trigger("high")) register_2 (.D(and_2_out), .en(CmpEnable), .Q(JE), .clk(Clock), .clr(Clear));
  Register #(.width(1), .trigger("high")) register_3 (.D(not_2_out), .en(CmpEnable), .Q(JAE), .clk(Clock), .clr(Clear));
  Register #(.width(1), .trigger("high")) register_4 (.D(and_3_out), .en(CmpEnable), .Q(JB), .clk(Clock), .clr(Clear));
  Register #(.width(1), .trigger("high")) register_5 (.D(or_1_out), .en(CmpEnable), .Q(JBE), .clk(Clock), .clr(Clear));
endmodule

// HCMP
module Half_Comparator (
  input  a,
  input  b,
  output EQ,
  output GT,
  output LT
);

  wire not_1_out, not_2_out;

  not not_1 (not_1_out, b);
  not not_2 (not_2_out, a);
  xnor xnor_1 (EQ, a, b);
  and and_1 (GT, a, not_1_out);
  and and_2 (LT, not_2_out, b);
endmodule

module ALU (
  input  [15:0] a,
  input  [15:0] b,
  input  ALUENABLE,
  input  AluControl,
  output [15:0] Result
);

  wire [15:0] and_1_out, n16_bit_adder_1_result;

  _16_Bit_Adder u_16_bit_adder_1 (.a(a), .b(b), .Result(n16_bit_adder_1_result));  // open: COut
  assign and_1_out = a & b;  // AND_Gate and_1, 16 bits wide
  Multiplexer #(.width(16)) multiplexer_1 (
    .in0(n16_bit_adder_1_result), .in1(and_1_out), .out(Result), .sel(AluControl), .en(ALUENABLE));
endmodule

// Register
module Register_File (
  input  [2:0] write,
  input  [2:0] read_register_1,
  input  [2:0] read_register_2,
  input  [15:0] input_data,
  input  Register_Write,
  input  clock,
  input  Reset,
  output [15:0] register1data,
  output [15:0] register2data
);

  wire and_1_out, and_2_out, and_3_out, and_4_out, and_5_out, and_6_out, and_7_out, and_8_out,
       decoder_1_out0, decoder_1_out1, decoder_1_out2, decoder_1_out3, decoder_1_out4, decoder_1_out5,
       decoder_1_out6, decoder_1_out7;
  wire [15:0] register_1_q, register_2_q, register_3_q, register_4_q, register_5_q, register_6_q,
       register_7_q, register_8_q;

  Decoder #(.select(3), .enable("false")) decoder_1 (
    .out0(decoder_1_out0), .out1(decoder_1_out1), .out2(decoder_1_out2), .out3(decoder_1_out3),
    .out4(decoder_1_out4), .out5(decoder_1_out5), .out6(decoder_1_out6), .out7(decoder_1_out7), .sel(write));
  and and_1 (and_1_out, decoder_1_out0, Register_Write);
  and and_2 (and_2_out, decoder_1_out1, Register_Write);
  and and_3 (and_3_out, decoder_1_out2, Register_Write);
  and and_4 (and_4_out, decoder_1_out3, Register_Write);
  Register #(.width(16), .trigger("high")) register_1 (
    .D(input_data), .en(and_1_out), .Q(register_1_q), .clk(clock), .clr(Reset));
  Register #(.width(16), .trigger("high")) register_2 (
    .D(input_data), .en(and_2_out), .Q(register_2_q), .clk(clock), .clr(Reset));
  Register #(.width(16), .trigger("high")) register_3 (
    .D(input_data), .en(and_3_out), .Q(register_3_q), .clk(clock), .clr(Reset));
  Register #(.width(16), .trigger("high")) register_4 (
    .D(input_data), .en(and_4_out), .Q(register_4_q), .clk(clock), .clr(Reset));
  and and_5 (and_5_out, decoder_1_out4, Register_Write);
  and and_6 (and_6_out, decoder_1_out5, Register_Write);
  and and_7 (and_7_out, decoder_1_out6, Register_Write);
  and and_8 (and_8_out, decoder_1_out7, Register_Write);
  Register #(.width(16), .trigger("high")) register_5 (
    .D(input_data), .en(and_5_out), .Q(register_5_q), .clk(clock), .clr(Reset));
  Register #(.width(16), .trigger("high")) register_6 (
    .D(input_data), .en(and_6_out), .Q(register_6_q), .clk(clock), .clr(Reset));
  Register #(.width(16), .trigger("high")) register_7 (
    .D(input_data), .en(and_7_out), .Q(register_7_q), .clk(clock), .clr(Reset));
  Register #(.width(16), .trigger("high")) register_8 (
    .D(input_data), .en(and_8_out), .Q(register_8_q), .clk(clock), .clr(Reset));
  Multiplexer #(.select(3), .width(16), .enable("false")) multiplexer_1 (
    .in0(register_1_q), .in1(register_2_q), .in2(register_3_q), .in3(register_4_q), .in4(register_5_q),
    .in5(register_6_q), .in6(register_7_q), .in7(register_8_q), .out(register1data), .sel(read_register_1));
  Multiplexer #(.select(3), .width(16), .enable("false")) multiplexer_2 (
    .in0(register_1_q), .in1(register_2_q), .in2(register_3_q), .in3(register_4_q), .in4(register_5_q),
    .in5(register_6_q), .in6(register_7_q), .in7(register_8_q), .out(register2data), .sel(read_register_2));
endmodule

// HS
module Half_Sub (
  input  a,
  input  b,
  output BOut,
  output D
);

  wire and_2_out, not_1_out, not_2_out;

  not not_1 (not_1_out, a);
  and and_1 (BOut, not_1_out, b);
  not not_2 (not_2_out, b);
  and and_2 (and_2_out, not_2_out, a);
  or or_1 (D, BOut, and_2_out);
endmodule

// FB
module Full_Sub (
  input  a,
  input  bin,
  input  b,
  output out_4,
  output BOut
);

  wire and_1_out, and_2_out, and_3_out, not_1_out, xor_1_out, xor_2_out;

  not not_1 (not_1_out, a);
  and and_1 (and_1_out, not_1_out, bin);
  and and_2 (and_2_out, not_1_out, b);
  xor xor_1 (xor_1_out, a, bin);
  xor xor_2 (xor_2_out, and_1_out, and_2_out);
  and and_3 (and_3_out, b, bin);
  xor xor_3 (out_4, xor_1_out, b);
  or or_1 (BOut, xor_2_out, and_3_out);
endmodule

// 10B
module _10_Bit_Adder (
  input  [9:0] a,
  input  [9:0] b,
  output [9:0] Result,
  output COut
);

  wire full_adder_1_cout, full_adder_2_cout, full_adder_3_cout, full_adder_4_cout, full_adder_5_cout,
       full_adder_6_cout, full_adder_7_cout, full_adder_8_cout, half_adder_1_cout;

  Half_Adder half_adder_1 (.b(b[0]), .a(a[0]), .Sum(Result[0]), .COut(half_adder_1_cout));
  Full_Adder full_adder_1 (.C_in(half_adder_1_cout), .a(b[1]), .b(a[1]), .S(Result[1]), .COut(full_adder_1_cout));
  Full_Adder full_adder_2 (.C_in(full_adder_1_cout), .a(b[2]), .b(a[2]), .S(Result[2]), .COut(full_adder_2_cout));
  Full_Adder full_adder_3 (.C_in(full_adder_2_cout), .a(b[3]), .b(a[3]), .S(Result[3]), .COut(full_adder_3_cout));
  Full_Adder full_adder_4 (.C_in(full_adder_3_cout), .a(b[4]), .b(a[4]), .S(Result[4]), .COut(full_adder_4_cout));
  Full_Adder full_adder_5 (.C_in(full_adder_4_cout), .a(b[5]), .b(a[5]), .S(Result[5]), .COut(full_adder_5_cout));
  Full_Adder full_adder_6 (.C_in(full_adder_5_cout), .a(b[6]), .b(a[6]), .S(Result[6]), .COut(full_adder_6_cout));
  Full_Adder full_adder_7 (.C_in(full_adder_6_cout), .a(b[7]), .b(a[7]), .S(Result[7]), .COut(full_adder_7_cout));
  Full_Adder full_adder_8 (.C_in(full_adder_7_cout), .a(b[8]), .b(a[8]), .S(Result[8]), .COut(full_adder_8_cout));
  Full_Adder full_adder_9 (.C_in(full_adder_8_cout), .a(b[9]), .b(a[9]), .S(Result[9]), .COut(COut));
endmodule

module _10_Bit_Sub (
  input  [9:0] b,
  input  [9:0] a,
  output [9:0] Result,
  output out_4
);

  wire full_sub_1_bout, full_sub_2_bout, full_sub_3_bout, full_sub_4_bout, full_sub_5_bout, full_sub_6_bout,
       full_sub_7_bout, full_sub_8_bout, half_sub_1_bout;

  Half_Sub half_sub_1 (.a(a[0]), .b(b[0]), .BOut(half_sub_1_bout), .D(Result[0]));
  Full_Sub full_sub_1 (.a(a[1]), .bin(half_sub_1_bout), .b(b[1]), .out_4(Result[1]), .BOut(full_sub_1_bout));
  Full_Sub full_sub_2 (.a(a[2]), .bin(full_sub_1_bout), .b(b[2]), .out_4(Result[2]), .BOut(full_sub_2_bout));
  Full_Sub full_sub_3 (.a(a[3]), .bin(full_sub_2_bout), .b(b[3]), .out_4(Result[3]), .BOut(full_sub_3_bout));
  Full_Sub full_sub_4 (.a(a[4]), .bin(full_sub_3_bout), .b(b[4]), .out_4(Result[4]), .BOut(full_sub_4_bout));
  Full_Sub full_sub_5 (.a(a[5]), .bin(full_sub_4_bout), .b(b[5]), .out_4(Result[5]), .BOut(full_sub_5_bout));
  Full_Sub full_sub_6 (.a(a[6]), .bin(full_sub_5_bout), .b(b[6]), .out_4(Result[6]), .BOut(full_sub_6_bout));
  Full_Sub full_sub_7 (.a(a[7]), .bin(full_sub_6_bout), .b(b[7]), .out_4(Result[7]), .BOut(full_sub_7_bout));
  Full_Sub full_sub_8 (.a(a[8]), .bin(full_sub_7_bout), .b(b[8]), .out_4(Result[8]), .BOut(full_sub_8_bout));
  Full_Sub full_sub_9 (.a(a[9]), .bin(full_sub_8_bout), .b(b[9]), .out_4(Result[9]), .BOut(out_4));
endmodule

// JUMP
module jmp (
  input  [9:0] JUMP_ADDRESS,
  input  ADDRSelect,
  input  Clear,
  input  Enable,
  input  Clock,
  input  BranchSignal,
  output [9:0] out_7
);

  wire [9:0] multiplexer_1_out, multiplexer_2_out, n10_bit_adder_1_result;

  Multiplexer #(.width(10)) multiplexer_1 (
    .in0(10'h1), .in1(JUMP_ADDRESS), .out(multiplexer_1_out), .sel(ADDRSelect));  // open: en
  _10_Bit_Adder u_10_bit_adder_1 (
    .a(multiplexer_1_out), .b(multiplexer_2_out), .Result(n10_bit_adder_1_result));  // open: COut
  Register #(.width(10), .trigger("falling")) register_1 (
    .D(n10_bit_adder_1_result), .en(Enable), .Q(out_7), .clk(Clock), .clr(Clear));
  Multiplexer #(.width(10)) multiplexer_2 (
    .in0(out_7), .in1({10{1'b0}}), .out(multiplexer_2_out), .sel(BranchSignal));  // open: en
endmodule

// cont
module Control_Unit (
  input  [15:0] Instruction,
  input  clock,
  input  JAIN,
  input  JEIN,
  input  JBIN,
  input  JAEIN,
  input  JBEIN,
  output [2:0] DR,
  output [2:0] SR1,
  output [2:0] SR2,
  output [5:0] IMM6,
  output dataMemWrite,
  output DataMemRead,
  output LDsignal,
  output STSignal,
  output [9:0] _10_BIT_ADDRESS,
  output \İnstRead ,
  output PCRead,
  output ALUcontrol,
  output IMM6SIGNAL,
  output CMPsig,
  output JumpSignal,
  output RegRead,
  output ALUEnable,
  output RegWrite
);

  wire ADD, ADD_ADDI, ADDI, ALUEnable1, ALUEnable2, ALUEnable3, ALUEnable4, AND, and_33_out, and_34_out,
       and_35_out, and_36_out, and_37_out, ANDI, CMP, decoder_2_out0, decoder_2_out1, decoder_2_out2,
       decoder_2_out3, decoder_2_out5, decoder_3_out0, decoder_3_out1, decoder_4_out0, decoder_4_out1, JA,
       JA_JE_JB_JAE_JBE, JAE, JB, JBE, JE, JMP, or_6_out, or_7_out, RegRead1, RegRead2, RegRead3, RegRead4,
       RegRead5, RegRead6, RegWrite1, RegWrite2, RegWrite3, RegWrite4, RegWrite5, Reset, Reset1, Reset2,
       Reset3, Reset4, Reset5, Reset6, Reset7, Reset8, State3, State4, State5, State6, State7, State8;
  wire [3:0] counter_1_q;

  Decoder #(.select(3), .enable("false")) decoder_1 (
    .out1(ADD_ADDI), .out2(ALUcontrol), .out3(LDsignal), .out4(STSignal), .out5(JMP), .out6(CMP),
    .out7(JA_JE_JB_JAE_JBE), .sel(Instruction[15:13]));  // open: out0
  Decoder #(.select(3), .enable("false")) decoder_2 (
    .out0(decoder_2_out0), .out1(decoder_2_out1), .out2(decoder_2_out2), .out3(decoder_2_out3),
    .out5(decoder_2_out5), .sel(Instruction[12:10]));  // open: out4, out6, out7
  Decoder #(.enable("false")) decoder_3 (.out0(decoder_3_out0), .out1(decoder_3_out1), .sel(Instruction[6]));
  Decoder #(.enable("false")) decoder_4 (.out0(decoder_4_out0), .out1(decoder_4_out1), .sel(Instruction[6]));
  or or_1 (ALUEnable, ALUEnable1, ALUEnable2, ALUEnable3, ALUEnable4);
  and and_1 (JA, decoder_2_out0, JA_JE_JB_JAE_JBE);
  and and_2 (JBE, decoder_2_out5, JA_JE_JB_JAE_JBE);
  Counter #(.width(4), .max('hf)) counter_1 (.Q(counter_1_q), .clk(clock), .clr(Reset));  // open: load, D, count, carry
  and and_3 (JE, decoder_2_out1, JA_JE_JB_JAE_JBE);
  and and_4 (JB, decoder_2_out2, JA_JE_JB_JAE_JBE);
  and and_5 (JAE, decoder_2_out3, JA_JE_JB_JAE_JBE);
  and and_6 (ADD, decoder_3_out0, ADD_ADDI);
  and and_7 (ADDI, decoder_3_out1, ADD_ADDI);
  Decoder #(.select(4), .enable("false")) decoder_5 (
    .out0(PCRead), .out1(\İnstRead ), .out2(State3), .out3(State4), .out4(State5), .out5(State6),
    .out6(State7), .out7(State8), .sel(counter_1_q));  // open: out8, out9, out10, out11, out12, out13, out14, out15
  and and_8 (AND, decoder_4_out0, ALUcontrol);
  and and_9 (ANDI, decoder_4_out1, ALUcontrol);
  or or_2 (RegWrite, RegWrite1, RegWrite2, RegWrite3, RegWrite4, RegWrite5);
  or or_3 (IMM6SIGNAL, ADDI, ANDI);
  and and_10 (RegRead1, State3, ADD);
  and and_11 (RegWrite1, State5, ADD);
  and and_12 (RegRead2, State3, AND);
  and and_13 (RegWrite2, State5, AND);
  or or_4 (RegRead, RegRead1, RegRead2, RegRead3, RegRead4, RegRead5, RegRead6);
  and and_14 (Reset1, State6, ADD);
  and and_15 (Reset2, State6, AND);
  and and_16 (ALUEnable1, State4, ADD);
  and and_17 (ALUEnable2, State4, AND);
  and and_18 (RegRead3, State3, ADDI);
  and and_19 (RegWrite3, State5, ADDI);
  or or_5 (Reset, Reset1, Reset2, Reset3, Reset4, Reset5, Reset6, Reset7, Reset8);
  and and_20 (RegRead4, State3, ANDI);
  and and_21 (RegWrite4, State5, ANDI);
  and and_22 (RegRead6, State3, CMP);
  and and_23 (CMPsig, State4, CMP);
  and and_24 (ALUEnable3, State4, ADDI);
  and and_25 (Reset3, State6, ADDI);
  and and_26 (ALUEnable4, State4, ANDI);
  and and_27 (Reset4, State5, ANDI);
  and and_28 (Reset8, State5, CMP);
  and and_29 (DataMemRead, State3, LDsignal);
  and and_30 (RegWrite5, State4, LDsignal);
  and and_31 (RegRead5, State3, STSignal);
  and and_32 (Reset6, State5, STSignal);
  and and_33 (and_33_out, JA, JAIN);
  and and_34 (and_34_out, JE, JEIN);
  and and_35 (and_35_out, JB, JBIN);
  and and_36 (and_36_out, JAE, JAEIN);
  and and_37 (and_37_out, JBEIN, JBE);
  and and_38 (Reset5, State5, LDsignal);
  and and_39 (dataMemWrite, State4, STSignal);
  and and_40 (Reset7, State4, or_6_out);
  or or_6 (or_6_out, JMP, JA, JE, JB, JAE, JBE);
  or or_7 (or_7_out, and_33_out, and_34_out, and_35_out, and_36_out, and_37_out);
  or or_8 (JumpSignal, JMP, or_7_out);

  assign _10_BIT_ADDRESS = Instruction[9:0];
  assign DR = Instruction[12:10];
  assign IMM6 = Instruction[5:0];
  assign SR1 = Instruction[9:7];
  assign SR2 = Instruction[2:0];

  // Other names for the same wires on the sheet: AND_ANDI = ALUcontrol; Clock1 = clock; dataMemRead1 = DataMemRead;
  //   dataMemWrite1 = dataMemWrite; LD = LDsignal; ST = STSignal; State1 = PCRead; State2 = \İnstRead 
endmodule
